// Logisim project Circuit.circ as structural Verilog: 1 circuit, main circuit main
module main (
  input  in_1,
  input  in_2,
  input  in_3,
  input  in_4,
  input  in_5,
  input  in_6,
  input  in_7,
  input  in_8
);

  wire adder_1_cout, adder_1_out, adder_2_cout, adder_2_out, adder_3_cout, adder_3_out, adder_4_cout,
       adder_4_out, adder_5_cout, adder_5_out, adder_6_cout, adder_6_out, adder_7_cout, adder_7_out,
       adder_8_cout, adder_8_out, not_1_out, not_2_out, not_3_out, not_4_out, not_5_out, not_6_out,
       not_7_out, not_8_out;

  not not_1 (not_1_out, in_1);
  LED led_1 (.in(adder_1_out));
  not not_2 (not_2_out, in_2);
  Adder #(.width(1)) adder_1 (.a(not_1_out), .b(adder_2_cout), .out(adder_1_out), .cout(adder_1_cout));  // open: cin
  LED led_2 (.in(adder_1_cout));
  LED led_3 (.in(adder_2_out));
  not not_3 (not_3_out, in_3);
  Adder #(.width(1)) adder_2 (.a(not_2_out), .b(adder_3_cout), .out(adder_2_out), .cout(adder_2_cout));  // open: cin
  LED led_4 (.in(adder_3_out));
  Adder #(.width(1)) adder_3 (.a(not_3_out), .b(adder_4_cout), .out(adder_3_out), .cout(adder_3_cout));  // open: cin
  LED led_5 (.in(adder_4_out));
  not not_4 (not_4_out, in_4);
  Adder #(.width(1)) adder_4 (.a(not_4_out), .b(adder_5_cout), .out(adder_4_out), .cout(adder_4_cout));  // open: cin
  LED led_6 (.in(adder_5_out));
  not not_5 (not_5_out, in_5);
  Adder #(.width(1)) adder_5 (.a(not_5_out), .b(adder_6_cout), .out(adder_5_out), .cout(adder_5_cout));  // open: cin
  LED led_7 (.in(adder_6_out));
  not not_6 (not_6_out, in_6);
  Adder #(.width(1)) adder_6 (.a(not_6_out), .b(adder_7_cout), .out(adder_6_out), .cout(adder_6_cout));  // open: cin
  LED led_8 (.in(adder_7_out));
  not not_7 (not_7_out, in_7);
  not not_8 (not_8_out, in_8);
  Adder #(.width(1)) adder_7 (.a(not_7_out), .b(adder_8_cout), .out(adder_7_out), .cout(adder_7_cout));  // open: cin
  LED led_9 (.in(adder_8_out));
  Adder #(.width(1)) adder_8 (.a(not_8_out), .b(1'b1), .out(adder_8_out), .cout(adder_8_cout));  // open: cin
endmodule
